// Logisim project master.circ as structural Verilog: 8 circuits, main circuit FullAdder
module HalfAdder (
  input  A,
  input  B,
  output Sum,
  output Cout
);

  xor xor_1 (Sum, A, B);
  and and_1 (Cout, A, B);
endmodule

module FullAdder (
  input  A,
  input  B,
  input  Cin,
  output Sum,
  output Cout
);

  wire and_1_out, and_2_out, and_3_out, xor_1_out;

  and and_1 (and_1_out, B, Cin);
  and and_2 (and_2_out, A, Cin);
  and and_3 (and_3_out, A, B);
  or or_1 (Cout, and_1_out, and_2_out, and_3_out);
  xor xor_1 (xor_1_out, A, B);
  xor xor_2 (Sum, xor_1_out, Cin);
endmodule

module FullSubtractor (
  input  A,
  input  B,
  input  Bin,
  output Sum,
  output Bout
);

  wire and_1_out, and_2_out, and_3_out, not_1_out, not_2_out, xor_1_out;

  and and_1 (and_1_out, B, Bin);
  not not_1 (not_1_out, A);
  and and_2 (and_2_out, not_1_out, Bin);
  not not_2 (not_2_out, A);
  and and_3 (and_3_out, not_2_out, B);
  or or_1 (Bout, and_1_out, and_2_out, and_3_out);
  xor xor_1 (xor_1_out, A, B);
  xor xor_2 (Sum, xor_1_out, Bin);
endmodule

module OnesComp (
  input  [3:0] A,
  output [3:0] R
);

  not not_1 (R[0], A[0]);
  not not_2 (R[1], A[1]);
  not not_3 (R[2], A[2]);
  not not_4 (R[3], A[3]);
endmodule

module TwosComp (
  input  [3:0] A,
  output [3:0] R
);

  wire fulladder_1_cout, fulladder_2_cout, fulladder_3_cout;
  wire [3:0] onescomp_1_r;

  OnesComp onescomp_1 (.A(A), .R(onescomp_1_r));
  FullAdder fulladder_1 (.A(1'b1), .B(onescomp_1_r[0]), .Sum(R[0]), .Cout(fulladder_1_cout));  // open: Cin
  FullAdder fulladder_2 (.A(onescomp_1_r[1]), .Cin(fulladder_1_cout), .Sum(R[1]), .Cout(fulladder_2_cout));  // open: B
  FullAdder fulladder_3 (.A(onescomp_1_r[2]), .Cin(fulladder_2_cout), .Sum(R[2]), .Cout(fulladder_3_cout));  // open: B
  FullAdder fulladder_4 (.A(onescomp_1_r[3]), .Cin(fulladder_3_cout), .Sum(R[3]));  // open: B, Cout
endmodule

module FourBitAdder (
  input  [3:0] Add1,
  input  [3:0] Add2,
  output [3:0] AddOut
);

  wire fulladder_2_cout, fulladder_3_cout, fulladder_4_cout;

  FullAdder fulladder_1 (.A(Add1[3]), .B(Add2[3]), .Cin(fulladder_2_cout), .Sum(AddOut[3]));  // open: Cout
  FullAdder fulladder_2 (.A(Add1[2]), .B(Add2[2]), .Cin(fulladder_3_cout), .Sum(AddOut[2]), .Cout(fulladder_2_cout));
  FullAdder fulladder_3 (.A(Add1[1]), .B(Add2[1]), .Cin(fulladder_4_cout), .Sum(AddOut[1]), .Cout(fulladder_3_cout));
  FullAdder fulladder_4 (.A(Add1[0]), .B(Add2[0]), .Sum(AddOut[0]), .Cout(fulladder_4_cout));  // open: Cin
endmodule

module FourBitSubtractor (
  input  [3:0] Subtract1,
  input  [3:0] Subtract2,
  output [3:0] SubtractOut
);

  wire fullsubtractor_2_bout, fullsubtractor_3_bout, fullsubtractor_4_bout;

  FullSubtractor fullsubtractor_1 (
    .A(Subtract1[3]), .B(Subtract2[3]), .Bin(fullsubtractor_2_bout), .Sum(SubtractOut[3]));  // open: Bout
  FullSubtractor fullsubtractor_2 (
    .A(Subtract1[2]), .B(Subtract2[2]), .Bin(fullsubtractor_3_bout), .Sum(SubtractOut[2]),
    .Bout(fullsubtractor_2_bout));
  FullSubtractor fullsubtractor_3 (
    .A(Subtract1[1]), .B(Subtract2[1]), .Bin(fullsubtractor_4_bout), .Sum(SubtractOut[1]),
    .Bout(fullsubtractor_3_bout));
  FullSubtractor fullsubtractor_4 (
    .A(Subtract1[0]), .B(Subtract2[0]), .Sum(SubtractOut[0]), .Bout(fullsubtractor_4_bout));  // open: Bin
endmodule

module SerialAdder (
);

  wire clock_1_out, d_ff_1_q, fulladder_1_cout, undriven, undriven_2;

  D_Flip_Flop d_ff_1 (.D(fulladder_1_cout), .clk(clock_1_out), .Q(d_ff_1_q));  // open: Qn, preset, reset
  Clock clock_1 (.out(clock_1_out));
  FullAdder fulladder_1 (.A(undriven), .B(undriven_2), .Cin(d_ff_1_q), .Cout(fulladder_1_cout));  // open: Sum
endmodule
